# Fritzing sketch Clock (saved by Fritzing 0.9.2b)
breadboards: 1

parts:
  MD03A1 = Dual VNH2SP30 Motor Driver [part_number=MD03A]
  M1 = DC Motor
  Part2 = Arduino Due (Rev2b)
  S1 = SPST Switch [package=switch-spdt-smd]
  M2 = DC Motor
  S2 = SPST Switch [package=switch-spdt-smd]

nets:
  N1: MD03A1.GND#136, MD03A1.GND#138, Part2.GND, S1.O, S2.O
  N2: MD03A1.+5V_(IN), Part2.5V
  N3: MD03A1.OUT_1A, M2.pin_1
  N4: MD03A1.OUT_1B, M2.pin_2
  N5: MD03A1.OUT_2A, M1.pin_1
  N6: MD03A1.OUT_2B, M1.pin_2
  N7: Part2.IOREF, S1.P, S2.P
  N8: Part2.D26, S1.S
  N9: Part2.D32, S2.S

notes:
  Connect to 12 V
  PIN 22 and PIN 23
  Encoder input DC1
  PIN 24 and PIN 25
  H-Bridge control A, B for DC1
  PIN 28 and PIN 29
  Encoder input DC2
  PIN 30 and PIN 31
  H-Bridge control A, B for DC1
